// Logisim project cpu.circ as structural Verilog: 7 circuits, main circuit main
module main (
  input  in_1,
  output [31:0] out_2,
  output out_3,
  output [4:0] out_4,
  output [31:0] out_5,
  output out_6,
  output [4:0] out_7,
  output [31:0] out_8
);

  wire ALUSrc, beq, clock_1_out, comparator_1_eq;
  wire [1:0] Branch, Data, EXTop, multiplexer_3_out, PCSrc, RegDst;
  wire [2:0] ALUop;
  wire [31:0] alu_1_result, dm_1_rd, GPR_rs, multiplexer_2_out, offset, PC_4;
  wire [31:5] shifter_1_out;

  Clock clock_1 (.out(clock_1_out));
  // Probe on out_2
  // Probe on out_2[15:0]
  IFU ifu_1 (
    .offset(offset), .instr(out_2), .CLK(clock_1_out), .RESET(in_1), .PCSrc(PCSrc), .index(out_2[25:0]),
    .gpr_rs(GPR_rs), .PC_4(PC_4));
  Controller controller_1 (
    .op(out_2[31:26]), .func(out_2[5:0]), .EXTop(EXTop), .ALUop(ALUop), .MemWrite(out_6), .RegWrite(out_3),
    .ALUSrc(ALUSrc), .Branch(Branch), .RegDst(RegDst), .data(Data));
  GRF grf_1 (
    .A1(out_2[25:21]), .A2(out_2[20:16]), .A3(out_4), .WD3(out_5), .RD1(GPR_rs), .RD2(out_8), .reset(in_1),
    .clk(clock_1_out), .we(out_3));
  Multiplexer #(.select(2), .width(5)) multiplexer_1 (
    .in0(out_2[15:11]), .in1(out_2[20:16]), .in2({5{1'b1}}), .out(out_4), .sel(RegDst));  // open: in3, en
  EXT ext_1 (.in_1(out_2[15:0]), .out_3(offset), .EXTop(EXTop));
  Multiplexer #(.width(32)) multiplexer_2 (
    .in0(out_8), .in1(offset), .out(multiplexer_2_out), .sel(ALUSrc));  // open: en
  Comparator #(.width(2)) comparator_1 (.a(Branch), .b(2'b01), .eq(comparator_1_eq));  // open: gt, lt
  ALU alu_1 (.A(GPR_rs), .B(multiplexer_2_out), .result(alu_1_result), .ALUop(ALUop));
  Comparator #(.width(32)) comparator_2 (.a({32{1'b0}}), .b(alu_1_result), .eq(beq));  // open: gt, lt
  Shifter #(.width(32), .shift("lr")) shifter_1 (.in(alu_1_result), .\dist (5'b00010), .out({shifter_1_out, out_7}));
  Multiplexer #(.width(2)) multiplexer_3 (.in0(2'b00), .in1(Branch), .out(multiplexer_3_out), .sel(beq));  // open: en
  Multiplexer #(.width(2)) multiplexer_4 (
    .in0(Branch), .in1(multiplexer_3_out), .out(PCSrc), .sel(comparator_1_eq));  // open: en
  DM dm_1 (.A(out_7), .WD(out_8), .RD(dm_1_rd), .CLK(clock_1_out), .WE(out_6), .reset(in_1));
  Multiplexer #(.select(2), .width(32)) multiplexer_5 (
    .in0(alu_1_result), .in1(dm_1_rd), .in2(offset), .in3(PC_4), .out(out_5), .sel(Data));  // open: en

  // Other names for the same wires on the sheet: MemAddr[4:0] = out_7; func[5:0] = out_2[5:0];
  //   imm[15:0] = out_2[15:0]; index[25:0] = out_2[25:0]; Instr[31:0] = out_2; MemData[31:0] = out_8;
  //   MemWrite = out_6; op[5:0] = out_2[31:26]; rd[4:0] = out_2[15:11]; RegAddr[4:0] = out_4; RegData[31:0] = out_5;
  //   RegWrite = out_3; reset = in_1; rs[4:0] = out_2[25:21]; rt[4:0] = out_2[20:16]; shamt[4:0] = out_2[10:6]
endmodule

module GRF (
  input  we,
  input  reset,
  input  clk,
  input  [4:0] A1,
  input  [4:0] A2,
  input  [4:0] A3,
  input  [31:0] WD3,
  output [31:0] RD1,
  output [31:0] RD2
);

  wire and_1_out, and_2_out, and_3_out, and_4_out, and_5_out, and_6_out, and_7_out, and_8_out, and_9_out,
       and_10_out, and_11_out, and_12_out, and_13_out, and_14_out, and_15_out, and_16_out, and_17_out,
       and_18_out, and_19_out, and_20_out, and_21_out, and_22_out, and_23_out, and_24_out, and_25_out,
       and_26_out, and_27_out, and_28_out, and_29_out, and_30_out, and_31_out, and_32_out, decoder_1_out0,
       decoder_1_out1, decoder_1_out2, decoder_1_out3, decoder_1_out4, decoder_1_out5, decoder_1_out6,
       decoder_1_out7, decoder_1_out8, decoder_1_out9, decoder_1_out10, decoder_1_out11, decoder_1_out12,
       decoder_1_out13, decoder_1_out14, decoder_1_out15, decoder_1_out16, decoder_1_out17, decoder_1_out18,
       decoder_1_out19, decoder_1_out20, decoder_1_out21, decoder_1_out22, decoder_1_out23, decoder_1_out24,
       decoder_1_out25, decoder_1_out26, decoder_1_out27, decoder_1_out28, decoder_1_out29, decoder_1_out30,
       decoder_1_out31;
  wire [31:0] register_1_q, register_2_q, register_3_q, register_4_q, register_5_q, register_6_q,
       register_7_q, register_8_q, register_9_q, register_10_q, register_11_q, register_12_q, register_13_q,
       register_14_q, register_15_q, register_16_q, register_17_q, register_18_q, register_19_q,
       register_20_q, register_21_q, register_22_q, register_23_q, register_24_q, register_25_q,
       register_26_q, register_27_q, register_28_q, register_29_q, register_30_q, register_31_q,
       register_32_q;

  Decoder #(.select(5)) decoder_1 (
    .out0(decoder_1_out0), .out1(decoder_1_out1), .out2(decoder_1_out2), .out3(decoder_1_out3),
    .out4(decoder_1_out4), .out5(decoder_1_out5), .out6(decoder_1_out6), .out7(decoder_1_out7),
    .out8(decoder_1_out8), .out9(decoder_1_out9), .out10(decoder_1_out10), .out11(decoder_1_out11),
    .out12(decoder_1_out12), .out13(decoder_1_out13), .out14(decoder_1_out14), .out15(decoder_1_out15),
    .out16(decoder_1_out16), .out17(decoder_1_out17), .out18(decoder_1_out18), .out19(decoder_1_out19),
    .out20(decoder_1_out20), .out21(decoder_1_out21), .out22(decoder_1_out22), .out23(decoder_1_out23),
    .out24(decoder_1_out24), .out25(decoder_1_out25), .out26(decoder_1_out26), .out27(decoder_1_out27),
    .out28(decoder_1_out28), .out29(decoder_1_out29), .out30(decoder_1_out30), .out31(decoder_1_out31),
    .sel(A3));  // open: en
  Register #(.width(32)) register_1 (.D(WD3), .en(and_1_out), .Q(register_1_q), .clk(clk), .clr(1'b1));
  Register #(.width(32)) register_2 (.D(WD3), .en(and_2_out), .Q(register_2_q), .clk(clk), .clr(reset));
  Register #(.width(32)) register_3 (.D(WD3), .en(and_3_out), .Q(register_3_q), .clk(clk), .clr(reset));
  Register #(.width(32)) register_4 (.D(WD3), .en(and_4_out), .Q(register_4_q), .clk(clk), .clr(reset));
  and and_1 (and_1_out, we, decoder_1_out0);
  and and_2 (and_2_out, we, decoder_1_out1);
  and and_3 (and_3_out, we, decoder_1_out2);
  and and_4 (and_4_out, we, decoder_1_out3);
  and and_5 (and_5_out, we, decoder_1_out4);
  and and_6 (and_6_out, we, decoder_1_out5);
  and and_7 (and_7_out, we, decoder_1_out6);
  and and_8 (and_8_out, we, decoder_1_out7);
  Register #(.width(32)) register_5 (.D(WD3), .en(and_5_out), .Q(register_5_q), .clk(clk), .clr(reset));
  Register #(.width(32)) register_6 (.D(WD3), .en(and_6_out), .Q(register_6_q), .clk(clk), .clr(reset));
  Register #(.width(32)) register_7 (.D(WD3), .en(and_7_out), .Q(register_7_q), .clk(clk), .clr(reset));
  Register #(.width(32)) register_8 (.D(WD3), .en(and_8_out), .Q(register_8_q), .clk(clk), .clr(reset));
  and and_9 (and_9_out, we, decoder_1_out8);
  and and_10 (and_10_out, we, decoder_1_out9);
  and and_11 (and_11_out, we, decoder_1_out10);
  and and_12 (and_12_out, we, decoder_1_out11);
  and and_13 (and_13_out, we, decoder_1_out12);
  and and_14 (and_14_out, we, decoder_1_out13);
  and and_15 (and_15_out, we, decoder_1_out14);
  and and_16 (and_16_out, we, decoder_1_out15);
  Register #(.width(32)) register_9 (.D(WD3), .en(and_9_out), .Q(register_9_q), .clk(clk), .clr(reset));
  Register #(.width(32)) register_10 (.D(WD3), .en(and_10_out), .Q(register_10_q), .clk(clk), .clr(reset));
  Register #(.width(32)) register_11 (.D(WD3), .en(and_11_out), .Q(register_11_q), .clk(clk), .clr(reset));
  Register #(.width(32)) register_12 (.D(WD3), .en(and_12_out), .Q(register_12_q), .clk(clk), .clr(reset));
  and and_17 (and_17_out, we, decoder_1_out16);
  and and_18 (and_18_out, we, decoder_1_out17);
  and and_19 (and_19_out, we, decoder_1_out18);
  and and_20 (and_20_out, we, decoder_1_out19);
  and and_21 (and_21_out, we, decoder_1_out20);
  and and_22 (and_22_out, we, decoder_1_out21);
  and and_23 (and_23_out, we, decoder_1_out22);
  and and_24 (and_24_out, we, decoder_1_out23);
  Register #(.width(32)) register_13 (.D(WD3), .en(and_13_out), .Q(register_13_q), .clk(clk), .clr(reset));
  Register #(.width(32)) register_14 (.D(WD3), .en(and_14_out), .Q(register_14_q), .clk(clk), .clr(reset));
  Register #(.width(32)) register_15 (.D(WD3), .en(and_15_out), .Q(register_15_q), .clk(clk), .clr(reset));
  Register #(.width(32)) register_16 (.D(WD3), .en(and_16_out), .Q(register_16_q), .clk(clk), .clr(reset));
  and and_25 (and_25_out, we, decoder_1_out24);
  and and_26 (and_26_out, we, decoder_1_out25);
  and and_27 (and_27_out, we, decoder_1_out26);
  and and_28 (and_28_out, we, decoder_1_out27);
  Register #(.width(32)) register_17 (.D(WD3), .en(and_17_out), .Q(register_17_q), .clk(clk), .clr(reset));
  Register #(.width(32)) register_18 (.D(WD3), .en(and_18_out), .Q(register_18_q), .clk(clk), .clr(reset));
  Register #(.width(32)) register_19 (.D(WD3), .en(and_19_out), .Q(register_19_q), .clk(clk), .clr(reset));
  Register #(.width(32)) register_20 (.D(WD3), .en(and_20_out), .Q(register_20_q), .clk(clk), .clr(reset));
  and and_29 (and_29_out, we, decoder_1_out28);
  and and_30 (and_30_out, we, decoder_1_out29);
  and and_31 (and_31_out, we, decoder_1_out30);
  and and_32 (and_32_out, we, decoder_1_out31);
  Register #(.width(32)) register_21 (.D(WD3), .en(and_21_out), .Q(register_21_q), .clk(clk), .clr(reset));
  Register #(.width(32)) register_22 (.D(WD3), .en(and_22_out), .Q(register_22_q), .clk(clk), .clr(reset));
  Register #(.width(32)) register_23 (.D(WD3), .en(and_23_out), .Q(register_23_q), .clk(clk), .clr(reset));
  Register #(.width(32)) register_24 (.D(WD3), .en(and_24_out), .Q(register_24_q), .clk(clk), .clr(reset));
  Register #(.width(32)) register_25 (.D(WD3), .en(and_25_out), .Q(register_25_q), .clk(clk), .clr(reset));
  Register #(.width(32)) register_26 (.D(WD3), .en(and_26_out), .Q(register_26_q), .clk(clk), .clr(reset));
  Register #(.width(32)) register_27 (.D(WD3), .en(and_27_out), .Q(register_27_q), .clk(clk), .clr(reset));
  Register #(.width(32)) register_28 (.D(WD3), .en(and_28_out), .Q(register_28_q), .clk(clk), .clr(reset));
  Register #(.width(32)) register_29 (.D(WD3), .en(and_29_out), .Q(register_29_q), .clk(clk), .clr(reset));
  Register #(.width(32)) register_30 (.D(WD3), .en(and_30_out), .Q(register_30_q), .clk(clk), .clr(reset));
  Register #(.width(32)) register_31 (.D(WD3), .en(and_31_out), .Q(register_31_q), .clk(clk), .clr(reset));
  Register #(.width(32)) register_32 (.D(WD3), .en(and_32_out), .Q(register_32_q), .clk(clk), .clr(reset));
  Multiplexer #(.select(5), .width(32)) multiplexer_1 (
    .in0(register_1_q), .in1(register_2_q), .in2(register_3_q), .in3(register_4_q), .in4(register_5_q),
    .in5(register_6_q), .in6(register_7_q), .in7(register_8_q), .in8(register_9_q), .in9(register_10_q),
    .in10(register_11_q), .in11(register_12_q), .in12(register_13_q), .in13(register_14_q),
    .in14(register_15_q), .in15(register_16_q), .in16(register_17_q), .in17(register_18_q),
    .in18(register_19_q), .in19(register_20_q), .in20(register_21_q), .in21(register_22_q),
    .in22(register_23_q), .in23(register_24_q), .in24(register_25_q), .in25(register_26_q),
    .in26(register_27_q), .in27(register_28_q), .in28(register_29_q), .in29(register_30_q),
    .in30(register_31_q), .in31(register_32_q), .out(RD1), .sel(A1));  // open: en
  Multiplexer #(.select(5), .width(32)) multiplexer_2 (
    .in0(register_1_q), .in1(register_2_q), .in2(register_3_q), .in3(register_4_q), .in4(register_5_q),
    .in5(register_6_q), .in6(register_7_q), .in7(register_8_q), .in8(register_9_q), .in9(register_10_q),
    .in10(register_11_q), .in11(register_12_q), .in12(register_13_q), .in13(register_14_q),
    .in14(register_15_q), .in15(register_16_q), .in16(register_17_q), .in17(register_18_q),
    .in18(register_19_q), .in19(register_20_q), .in20(register_21_q), .in21(register_22_q),
    .in22(register_23_q), .in23(register_24_q), .in24(register_25_q), .in25(register_26_q),
    .in26(register_27_q), .in27(register_28_q), .in28(register_29_q), .in29(register_30_q),
    .in30(register_31_q), .in31(register_32_q), .out(RD2), .sel(A2));  // open: en

  // Notes on the sheet:
  //   0-3
  //   4-7
  //   8-11
  //   12-15
  //   16-19
  //   20-23
  //   24-27
  //   28-31
endmodule

module DM (
  input  reset,
  input  CLK,
  input  WE,
  input  [4:0] A,
  input  [31:0] WD,
  output [31:0] RD
);

  RAM #(.addrWidth(5), .dataWidth(32), .bus("separate")) ram_1 (
    .addr(A), .din(WD), .data(RD), .str(WE), .clk(CLK), .clr(reset));  // open: sel, ld
endmodule

module ALU (
  input  [31:0] A,
  input  [31:0] B,
  input  [2:0] ALUop,
  output [31:0] result
);

  wire comparator_1_eq, comparator_1_gt, comparator_1_lt;
  wire [31:0] adder_1_out, controlled_buffer_1_out, or_1_out, subtractor_1_out;

  Comparator #(.width(32)) comparator_1 (
    .a(A), .b(B), .gt(comparator_1_gt), .eq(comparator_1_eq), .lt(comparator_1_lt));
  assign controlled_buffer_1_out = comparator_1_gt ? 32'h1 : 32'bz;  // Controlled_Buffer controlled_buffer_1
  assign controlled_buffer_1_out = comparator_1_lt ? {32{1'b1}} : 32'bz;  // Controlled_Buffer controlled_buffer_2
  Adder #(.width(32)) adder_1 (.a(A), .b(B), .out(adder_1_out));  // open: cin, cout
  Subtractor #(.width(32)) subtractor_1 (.a(A), .b(B), .out(subtractor_1_out));  // open: bin, bout
  assign or_1_out = A | B;  // OR_Gate or_1, 32 bits wide
  assign controlled_buffer_1_out = comparator_1_eq ? {32{1'b0}} : 32'bz;  // Controlled_Buffer controlled_buffer_3
  Multiplexer #(.select(3), .width(32)) multiplexer_1 (
    .in0(adder_1_out), .in1(subtractor_1_out), .in2(or_1_out), .in3(controlled_buffer_1_out), .out(result),
    .sel(ALUop));  // open: in4, in5, in6, in7, en

  // Notes on the sheet:
  //   000加，001减，010或，011大小比较
endmodule

module EXT (
  input  [15:0] in_1,
  input  [1:0] EXTop,
  output [31:0] out_3
);

  wire [31:0] bit_extender_1_out, bit_extender_2_out;

  assign bit_extender_1_out = {{16{in_1[15]}}, in_1};  // Bit_Extender bit_extender_1
  assign bit_extender_2_out = {{16{1'b0}}, in_1};  // Bit_Extender bit_extender_2
  Multiplexer #(.select(2), .width(32)) multiplexer_1 (
    .in0(bit_extender_1_out), .in1(bit_extender_2_out), .in2({in_1, {16{1'b0}}}), .out(out_3), .sel(EXTop));  // open: in3, en

  // Notes on the sheet:
  //   00符号拓展，01零拓展，10加载高位，11无所谓
endmodule

module IFU (
  input  CLK,
  input  RESET,
  input  [1:0] PCSrc,
  input  [31:0] offset,
  input  [25:0] index,
  input  [31:0] gpr_rs,
  output [31:0] instr,
  output [31:0] PC_4
);

  wire [31:0] adder_2_out, multiplexer_1_out, PC_q;

  Register #(.width(32)) PC (.D(multiplexer_1_out), .Q(PC_q), .clk(CLK), .clr(RESET));  // open: en
  Adder #(.width(32)) adder_1 (.a(PC_q), .b(32'h1), .out(PC_4));  // open: cin, cout
  ROM #(.addrWidth(5), .dataWidth(32)) rom_1 (.addr(PC_q[4:0]), .data(instr));  // open: sel
  Adder #(.width(32)) adder_2 (.a(offset), .b(PC_4), .out(adder_2_out));  // open: cin, cout
  Multiplexer #(.select(2), .width(32)) multiplexer_1 (
    .in0(PC_4), .in1(adder_2_out), .in2({2'b00, PC_q[31:28], index}), .in3(gpr_rs), .out(multiplexer_1_out),
    .sel(PCSrc));  // open: en

  // Notes on the sheet:
  //   contents of rom_1 (hex, n*v repeats v):
  //   c000002 34090002 34080001 3e00008
endmodule

module Controller (
  input  [5:0] op,
  input  [5:0] func,
  output [1:0] Branch,
  output [1:0] EXTop,
  output [2:0] ALUop,
  output MemWrite,
  output RegWrite,
  output [1:0] RegDst,
  output ALUSrc,
  output [1:0] data
);

  wire ADDU, and_1_out, and_8_out, and_9_out, and_10_out, BEQ, JR, LW, not_1_out, not_2_out, not_3_out,
       not_4_out, not_5_out, not_6_out, not_7_out, not_8_out, not_9_out, not_10_out, not_11_out, not_12_out,
       SUBU;

  not not_1 (not_1_out, op[5]);
  not not_2 (not_2_out, op[4]);
  not not_3 (not_3_out, op[2]);
  not not_4 (not_4_out, op[3]);
  not not_5 (not_5_out, op[1]);
  not not_6 (not_6_out, op[0]);
  and and_1 (and_1_out, not_6_out, not_5_out, not_3_out, not_4_out, not_2_out, not_1_out);
  and and_2 (EXTop[0], op[0], not_5_out, op[2], op[3], not_2_out, not_1_out);
  and and_3 (LW, op[0], op[1], not_3_out, not_4_out, not_2_out, op[5]);
  and and_4 (MemWrite, op[0], op[1], not_3_out, op[3], not_2_out, op[5]);
  and and_5 (BEQ, not_6_out, not_5_out, op[2], not_4_out, not_2_out, not_1_out);
  and and_6 (EXTop[1], op[0], op[1], op[2], op[3], not_2_out, not_1_out);
  and and_7 (RegDst[1], op[0], op[1], not_3_out, not_4_out, not_2_out, not_1_out);
  or or_1 (Branch[0], BEQ, JR);
  or or_2 (Branch[1], RegDst[1], JR);
  or or_3 (ALUop[0], SUBU, BEQ);
  or or_4 (ALUop[1], EXTop[0], BEQ);
  or or_5 (RegWrite, EXTop[1], ADDU, SUBU, EXTop[0], LW, RegDst[1]);
  or or_6 (RegDst[0], EXTop[0], LW, EXTop[1]);
  or or_7 (ALUSrc, EXTop[0], MemWrite, LW);
  or or_8 (data[0], LW, RegDst[1]);
  or or_9 (data[1], EXTop[1], RegDst[1]);
  not not_7 (not_7_out, func[5]);
  not not_8 (not_8_out, func[4]);
  not not_9 (not_9_out, func[3]);
  not not_10 (not_10_out, func[2]);
  not not_11 (not_11_out, func[1]);
  not not_12 (not_12_out, func[0]);
  and and_8 (and_8_out, func[0], not_11_out, not_10_out, not_9_out, not_8_out, func[5]);
  and and_9 (and_9_out, func[0], func[1], not_10_out, not_9_out, not_8_out, func[5]);
  and and_10 (and_10_out, not_12_out, not_11_out, not_10_out, func[3], not_8_out, not_7_out);
  and and_11 (ADDU, and_1_out, and_8_out);
  and and_12 (SUBU, and_1_out, and_9_out);
  and and_13 (JR, and_1_out, and_10_out);

  assign ALUop[2] = 1'b0;

  // Other names for the same wires on the sheet: ORI = EXTop[0]; LUI = EXTop[1]; JAL = RegDst[1]; SW = MemWrite
endmodule
